# Fritzing sketch nor (saved by Fritzing 0.9.3b)
breadboards: 1

parts:
  Part1 = Arduino Uno (Rev3)
  S1 = Pushbutton [package="[THT]"]
  R1 = Resistor [tolerance=±5% resistance=220 package=THT]
  Part2 = HC-SR04 Ultrasonic Rangemeter
  LCD2 = LCD screen
  R2 = Resistor [tolerance=±5% resistance=220 package=THT]
  R3 = Rotary Potentiometer (Large) [maximum_resistance=100kΩ package=THT]

nets:
  N1: Part1.D8, S1.Pin_1, S1.Pin_2, R1.Pin_1
  N2: Part1.D9_PWM, Part2.Trig
  N3: Part1.D10_PWM/SS, Part2.Echo
  N4: Part1.D11_PWM/MOSI, LCD2.E
  N5: Part1.D12/MISO, LCD2.RS
  N6: Part1.D2, LCD2.DB7
  N7: Part1.D3_PWM, LCD2.DB6
  N8: Part1.D4, LCD2.DB5
  N9: Part1.D5_PWM, LCD2.DB3, LCD2.DB4
  5V: Part1.5V, S1.Pin_3, S1.Pin_4, Part2.VCC, LCD2.VDD
  GND: Part1.GND, R1.Pin_0, Part2.GND, LCD2.VSS, LCD2.R/W
  N10: LCD2.V0, R3.wiper
  N11: LCD2.LED+, R2.Pin_0
  N12: LCD2.LED-, R3.leg2
  N13: R2.Pin_1, R3.leg1

// code stored in the sketch: deneneme.ino
#include <LiquidCrystal.h>
#include<Wire.h>
#include<LcdBarGraphI2C.h>
LiquidCrystal_I2C lcd(0x27, 2, 1, 0, 4, 5, 6, 7, 3, POSITIVE); 
LcdBarGraphI2C lbg(&lcd, 16, 0, 1);

//LiquidCrystal lcd(4,6,10,11,12,13);

long duration,distance;

void setup() {
  // put your setup code here, to run once:
  lcd.begin(16,2);
  pinMode(8,INPUT);
  pinMode(3,OUTPUT);
  pinMode(2,INPUT);
}

void loop() {
  // put your main code here, to run repeatedly:
  if(digitalRead(8) == HIGH){
    digitalWrite(3,LOW);
    delayMicroseconds(2);
    digitalWrite(3,HIGH);
    delayMicroseconds(10);
    digitalWrite(3,LOW);
    duration = pulseIn(2,HIGH);
    distance = (duration/2) / 29.1;
    
    lcd.setCursor(0,0);
    lcd.print(distance);
    lcd.setCursor(5,0);
    lcd.print("cm");
		
				




    delay(5000);  // Ultrasonic sensor code by jsvester on Instructables at http://www.instructables.com/id/Simple-Arduino-and-HC-SR04-Example/?ALLSTEPS
  }
  else{
    lcd.clear();
  }
}

// code stored in the sketch: v1.ino

#include <LCD.h>
#include <LiquidCrystal.h>
#include <LiquidCrystal_I2C.h>
#include<Wire.h>
#include<LCD.h>
#include<LcdBarGraphI2C.h>

LiquidCrystal_I2C lcd(0x27, 2, 1, 0, 4, 5, 6, 7, 3, POSITIVE); 
LcdBarGraphI2C lbg(&lcd, 16, 0, 1); // Creates an LCD Bargraph object.

const int trigPin = 9;
const int echoPin = 10;
long duration;
int distance;
#define max_distance 30  // Maximum distance we want to ping for (in centimeters).

void setup() 
{
  lcd.begin(16,2); // Initializes the interface to the LCD screen
  lcd.backlight();
  pinMode(8,INPUT);
  pinMode(trigPin, OUTPUT);
  pinMode(echoPin, INPUT);
}

void loop() 
{
  // Write a pulse to the HC-SR04 Trigger Pin
  if(digitalRead(8) == HIGH){
  digitalWrite(trigPin, LOW);
  delayMicroseconds(2);
  digitalWrite(trigPin, HIGH);
  delayMicroseconds(10);
  digitalWrite(trigPin, LOW);
  
  // Measure the response from the HC-SR04 Echo Pin
  duration = pulseIn(echoPin, HIGH);
  
  // Determine distance from duration
  // Use 343 metres per second as speed of sound
  distance= duration*0.034/2;
  
  // Prints "Distance: " on the first line of the LCD
  lcd.setCursor(0,0);
  lcd.print("Distance: "); 
  lcd.print(distance);
  lcd.print(" cm");

  // Draws bargraph on the second line of the LCD
  lcd.setCursor(0,1);
  lbg.drawValue(distance, max_distance);
  delay(500);
}
}
